// Digital circuit Bus.dig as structural Verilog
module Bus (
  input  clk,
  output [7:0] Data
);

  wire decoder_1_out_0, decoder_1_out_1, decoder_1_out_2, decoder_1_out_3;
  wire [4:0] Address_out;

  Counter #(.Bits(5)) Address (.en(clk), .C(1'b0), .out(Address_out));  // open: clr, ovf
  Decoder #(.Selector_Bits(2)) decoder_1 (
    .sel(Address_out[4:3]), .out_0(decoder_1_out_0), .out_1(decoder_1_out_1), .out_2(decoder_1_out_2),
    .out_3(decoder_1_out_3));
  ROM #(.Bits(8), .Addr_Bits(3)) rom_1 (.A(Address_out[2:0]), .sel(decoder_1_out_0), .D(Data));
  ROM #(.Bits(8), .Addr_Bits(3)) rom_2 (.A(Address_out[2:0]), .sel(decoder_1_out_1), .D(Data));
  ROM #(.Bits(8), .Addr_Bits(3)) rom_3 (.A(Address_out[2:0]), .sel(decoder_1_out_2), .D(Data));
  ROM #(.Bits(8), .Addr_Bits(3)) rom_4 (.A(Address_out[2:0]), .sel(decoder_1_out_3), .D(Data));

  // Notes on the sheet:
  //   clk: Hz: 2
  //   contents of rom_1 (hex, n*v repeats v):
  //   8
  //   1
  //   2
  //   3
  //   4
  //   5
  //   6
  //   7
  //   8
  //   0
  //   contents of rom_2 (hex, n*v repeats v):
  //   8
  //   9
  //   10
  //   11
  //   12
  //   13
  //   14
  //   15
  //   16
  //   0
  //   contents of rom_3 (hex, n*v repeats v):
  //   8
  //   17
  //   18
  //   19
  //   20
  //   21
  //   22
  //   23
  //   24
  //   0
  //   contents of rom_4 (hex, n*v repeats v):
  //   8
  //   25
  //   26
  //   27
  //   28
  //   29
  //   30
  //   31
  //   32
  //   0
endmodule
