// Digital circuit Processor.dig as structural Verilog
module Processor (
  input  Clock
);

  wire alu_1_p6, alu_1_p7, alu_1_p8, control_1_p2, control_1_p7, control_1_p8, control_1_p9, control_1_p10,
       control_1_p11, control_1_p12, control_1_p13, gpo_1_p5, gpo_1_p6, gpo_1_p7, gpo_1_p8, gpo_1_p9,
       gpo_1_p10, gpo_1_p11, gpo_1_p12, gpo_1_p13, gpo_1_p14, gpo_1_p15, gpo_1_p16, gpo_1_p17, gpo_1_p18,
       gpo_1_p19, gpo_1_p20, imreg_1_p2, pc_1_p3, pc_1_p4, register_1_p5, register_1_p6, register_1_p7;
  wire [2:0] control_1_p6;
  wire [3:0] rom_1_d, rom_1_d_2;
  wire [6:0] rom_1_d_4;
  wire [8:8] rom_1_d_3;
  wire [15:0] driver_1_out, imreg_1_p4, multiplexer_1_out, multiplexer_2_out, pc_1_p1, pc_1_p5, pc_1_p6,
       register_1_p8, register_1_p9, signext_1_p2, signext_1_p3, signext_1_p4;

  // PC pc_1: pin names not known; wires that end beside it: pc_1_p1, Clock, pc_1_p3, pc_1_p4, pc_1_p5, pc_1_p6
  ROM #(.Bits(16), .Addr_Bits(16)) rom_1 (.A(pc_1_p6), .sel(1'b1), .D({rom_1_d_4, rom_1_d_3[8], rom_1_d_2, rom_1_d}));
  assign driver_1_out = control_1_p2 ? pc_1_p5 : 16'bz;  // Driver driver_1
  // Register register_1: pin names not known; wires that end beside it: driver_1_out, Clock, rom_1_d, rom_1_d_2, register_1_p5, register_1_p6, register_1_p7, register_1_p8, register_1_p9
  // ImReg imreg_1: pin names not known; wires that end beside it: {rom_1_d_4, rom_1_d_3[8], rom_1_d_2, rom_1_d}, imreg_1_p2, Clock, imreg_1_p4
  // Control control_1: pin names not known; wires that end beside it: rom_1_d_4, control_1_p2, register_1_p5, imreg_1_p2, pc_1_p3, control_1_p6, control_1_p7, control_1_p8, control_1_p9, control_1_p10, control_1_p11, control_1_p12, control_1_p13
  // Probe R0 on register_1_p6
  // SignExt signext_1: pin names not known; wires that end beside it: {rom_1_d_4, rom_1_d_3[8], rom_1_d_2, rom_1_d}, signext_1_p2, signext_1_p3, signext_1_p4
  // Probe R1 on register_1_p7
  Multiplexer #(.Selector_Bits(3), .Bits(16)) multiplexer_1 (
    .sel(control_1_p6), .in_0(register_1_p9), .in_1(imreg_1_p4), .in_2({16{1'b0}}), .in_3(16'hff),
    .in_4(16'hfff), .in_5(signext_1_p2), .in_6(signext_1_p3), .in_7(signext_1_p4), .out(multiplexer_1_out));
  Multiplexer #(.Bits(16)) multiplexer_2 (
    .sel(control_1_p7), .in_0(register_1_p8), .in_1(register_1_p9), .out(multiplexer_2_out));
  // ALU alu_1: pin names not known; wires that end beside it: multiplexer_2_out, multiplexer_1_out, control_1_p9, Clock, pc_1_p1, alu_1_p6, alu_1_p7, alu_1_p8
  assign driver_1_out = control_1_p8 ? pc_1_p1 : 16'bz;  // Driver driver_2
  // Branch branch_1: pin names not known; wires that end beside it: alu_1_p6, alu_1_p7, alu_1_p8, control_1_p10, pc_1_p4
  RAMDualPort #(.Bits(16), .Addr_Bits(16)) ramdualport_1 (
    .A(pc_1_p1), .Din(register_1_p9), .str(control_1_p11), .C(Clock), .ld(control_1_p12), .D(driver_1_out));
  // GPO gpo_1: pin names not known; wires that end beside it: pc_1_p1, register_1_p9, Clock, control_1_p13, gpo_1_p5, gpo_1_p6, gpo_1_p7, gpo_1_p8, gpo_1_p9, gpo_1_p10, gpo_1_p11, gpo_1_p12, gpo_1_p13, gpo_1_p14, gpo_1_p15, gpo_1_p16, gpo_1_p17, gpo_1_p18, gpo_1_p19, gpo_1_p20
  LED led_1 (.in(gpo_1_p5));
  LED led_2 (.in(gpo_1_p6));
  LED led_3 (.in(gpo_1_p7));
  LED led_4 (.in(gpo_1_p8));
  LED led_5 (.in(gpo_1_p9));
  LED led_6 (.in(gpo_1_p10));
  LED led_7 (.in(gpo_1_p11));
  LED led_8 (.in(gpo_1_p12));
  LED led_9 (.in(gpo_1_p13));
  LED led_10 (.in(gpo_1_p14));
  LED led_11 (.in(gpo_1_p15));
  LED led_12 (.in(gpo_1_p16));
  LED led_13 (.in(gpo_1_p17));
  LED led_14 (.in(gpo_1_p18));
  LED led_15 (.in(gpo_1_p19));
  LED led_16 (.in(gpo_1_p20));

  // Notes on the sheet:
  //   Clock: Hz: 5
  //   contents of rom_1 (hex, n*v repeats v):
  //   34
  //   5380
  //   8417
  //   5365
  //   19695
  //   28163
  //   20992
  //   31744
  //   28664
  //   15362
  //   23573
  //   8417
  //   19680
  //   8193
  //   8417
  //   5617
  //   19695
  //   28663
  //   19998
  //   6369
  //   8417
  //   19680
  //   8210
  //   513
  //   8417
  //   32796
  //   4848
  //   19695
  //   28652
  //   19998
  //   6369
  //   1025
  //   20222
  //   6369
  //   27151
  //   16
endmodule
