// Digital circuit ProcessorIntr.dig as structural Verilog
// Simple processor based on the MIPS architecture. 
// It is a Harvard single-cycle CPU.
// It has an interrupt controller: A rising edge at the 
// input intr triggers an interrupt. The fixed address 0x1000 
// is called. The ISR must be at this address.
// {{de Einfacher Prozessor, der an die MIPS-Architektur 
// angelehnt ist. Es handelt sich um eine Harvard 
// Single-Cycle CPU. Er verfügt über einen Interrupt 
// Controller: Durch eine steigende Flanke am Eingang intr 
// wird ein Interrupt ausgelöst. Dabei wird die feste 
// Adresse 0x1000 angesprungen.
// An dieser Adresse muss sich die ISR befinden.}}
module ProcessorIntr (
  input  C,
  input  intr,
  output [15:0] D,
  output [15:0] A,
  output ioR,
  output ioW
);

  wire abs, alu2D, alu_1_carry, alu_1_neg, alu_1_zero, branch_1_jmp, flagsrw_1_p1, flagsrw_1_p2,
       flagsrw_1_p3, flagsrw_1_p4, iEn, imm, ld, muxA, reti, sf, src2D, st, stPC, WE;
  wire [2:0] br, muxB;
  wire [4:0] aluOp;
  wire [15:0] imreg_1_imm, multiplexer_1_out, multiplexer_2_out, pcintr_1_next, pcintr_1_pc,
       register_1_rdest, register_1_rsrc, ROM_d, signext_1__5d, signext_1__5s, signext_1__9sd;

  PCintr pcintr_1 (
    .ALU(A), .C(C), .abs(abs), .intr(iEn), .reti(reti), .rel(branch_1_jmp), .Next(pcintr_1_next),
    .PC(pcintr_1_pc));
  ROM #(.AddrBits(16), .isProgramMemory("true"), .Bits(16), .Addr_Bits(16)) ROM (
    .A(pcintr_1_pc), .sel(1'b1), .D(ROM_d));
  assign D = stPC ? pcintr_1_next : 16'bz;  // Driver driver_1
  ControlIntr controlintr_1 (
    .Op(ROM_d[15:9]), .stPC(stPC), .WE(WE), .imm(imm), .absJmp(abs), .muxB(muxB), .src2D(src2D), .muxA(muxA),
    .alu2D(alu2D), .aluOp(aluOp), .storeFlags(sf), .Branch(br), .ramSt(st), .ramLd(ld), .ioW(ioW), .ioR(ioR),
    .reti(reti));
  Register register_1 (
    .WD(D), .C(C), .src(ROM_d[3:0]), .dest(ROM_d[7:4]), .WE(WE), .Rdest(register_1_rdest),
    .Rsrc(register_1_rsrc));
  ImReg imreg_1 (.inst(ROM_d), .en(imm), .C(C), .imm(imreg_1_imm));
  SignExt signext_1 (.inst(ROM_d), ._5S(signext_1__5s), ._9SD(signext_1__9sd), ._5D(signext_1__5d));
  assign D = src2D ? register_1_rsrc : 16'bz;  // Driver driver_2
  Multiplexer #(.Bits(16)) multiplexer_1 (
    .sel(muxA), .in_0(register_1_rdest), .in_1(register_1_rsrc), .out(multiplexer_1_out));
  Multiplexer #(.Selector_Bits(3), .Bits(16)) multiplexer_2 (
    .sel(muxB), .in_0(register_1_rsrc), .in_1(imreg_1_imm), .in_2({16{1'b0}}), .in_3({16{1'b0}}),
    .in_4({16{1'b0}}), .in_5(signext_1__5s), .in_6(signext_1__9sd), .in_7(signext_1__5d),
    .out(multiplexer_2_out));
  Branch branch_1 (.Z(flagsrw_1_p3), .N(flagsrw_1_p2), .C(flagsrw_1_p1), .ctrl(br), .jmp(branch_1_jmp));
  ALU alu_1 (
    .A(multiplexer_1_out), .B(multiplexer_2_out), .Op(aluOp), .Y(A), .Zero(alu_1_zero), .Neg(alu_1_neg),
    .Carry(alu_1_carry), .Ci(flagsrw_1_p1));
  Interrupt interrupt_1 (.nie(flagsrw_1_p4), .C(C), .imm(imm), .reti(reti), .intr(intr), .iEn(iEn));
  // FlagsRW flagsrw_1: pin names not known; wires that end beside it: flagsrw_1_p1, flagsrw_1_p2, flagsrw_1_p3, flagsrw_1_p4, D, ioW, ioR, A, sf, C, alu_1_carry, alu_1_neg, alu_1_zero
  assign D = alu2D ? A : 16'bz;  // Driver driver_3
  RAMSinglePort #(.AddrBits(16), .Bits(16), .Addr_Bits(16)) ramsingleport_1 (.A(A), .str(st), .C(C), .ld(ld), .D(D));

  // Notes on the sheet:
  //   C: Hz: 500000
  //   D: data bus {{de Datenbus}}
  //   A: address bus {{de Adressbus}}
  //   ioR: io read {{de io read}}
  //   ioW: io write {{de io write}}
  //   intr: Interrupt input. If this line goes high, an interrupt 
  //   is triggered. The ISR must be at address 0x1000.
  //   {{de Interrupt Eingang. Geht diese Leitung auf high wird ein
  //   Interrupt ausgelöst. Die ISR muss sich an Adresse 
  //   0x1000 befinden.}}
  //   contents of ROM (hex, n*v repeats v):
  //   6e10,0,ffff,59e0,7800,fffe,59e0,20e2,790e,73f0,18e2,fffe,5b0e,7200,ffff,5b0e,7e00,
  //   1401,7350,3e00,65fd,8000,1300,7350,4000,65fd,6ff6
endmodule
